# Fritzing sketch schema (saved by Fritzing 0.8.7b)
circuit board: 8.46667cm x 5.64444cm
breadboards: 1

parts:
  Composant1 = Arduino Uno (Rev3)
  LED1 = LED - 5mm [color="Green (565nm)" package="5 mm [THT]"]
  R1 = Resistor [tolerance=±5% resistance=220 package=THT]
  R2 = Resistor [tolerance=±5% resistance=220 package=THT]
  LED2 = LED - 5mm [color="Orange (605nm)" package="5 mm [THT]"]
  LED3 = LED - 5mm [color="Yellow (592nm)" package="5 mm [THT]"]
  LED4 = LED - 5mm [color="Red (633nm)" package="5 mm [THT]"]
  R3 = Resistor [tolerance=±5% resistance=220 package=THT]
  R4 = Resistor [tolerance=±5% resistance=220 package=THT]
  SPKR1 = Loudspeaker

nets:
  N1: Composant1.D8, SPKR1.pin2
  N2: Composant1.GND, LED1.cathode, LED2.cathode, LED3.cathode, LED4.cathode, SPKR1.pin1
  N3: Composant1.D4, R4.Pin_1
  N4: Composant1.D5_PWM, R3.Pin_1
  N5: Composant1.D6_PWM, R2.Pin_1
  N6: Composant1.D7, R1.Pin_1
  N7: LED1.anode, R1.Pin_0
  N8: R2.Pin_0, LED2.anode
  N9: LED3.anode, R3.Pin_0
  N10: LED4.anode, R4.Pin_0
